// Logisim project stack_logical_normal.circ as structural Verilog: 17 circuits, main circuit main
module main (
  input  CLK,
  input  RESET,
  input  [1:0] COMMAND,
  input  [2:0] INDEX,
  input  [3:0] IO_DATA_in,
  output [3:0] IO_DATA_out
);

  wire [3:0] stack_1_d0, stack_1_d1, stack_1_d2, stack_1_d3, stack_1_d4;

  // Probe on stack_1_d0
  stack stack_1 (
    .CLK(CLK), .RESET(RESET), .COMMAND(COMMAND), .INDEX(INDEX), .IO_DATA_in(IO_DATA_in), .d0(stack_1_d0),
    .d1(stack_1_d1), .d2(stack_1_d2), .d3(stack_1_d3), .d4(stack_1_d4), .IO_DATA_out(IO_DATA_out));
  // Probe on stack_1_d1
  // Probe on stack_1_d2
  // Probe on stack_1_d3
  // Probe on stack_1_d4
endmodule

module stack (
  input  CLK,
  input  RESET,
  input  [1:0] COMMAND,
  input  [2:0] INDEX,
  input  [3:0] IO_DATA_in,
  output [3:0] d0,
  output [3:0] d1,
  output [3:0] d2,
  output [3:0] d3,
  output [3:0] d4,
  output [3:0] IO_DATA_out
);

  wire and_1_out, and_3_out, get_command_1_push, not_1_out, or_1_out, transmission_1_p2;
  wire [2:0] and_2_out, inc_dec_pointer_1_res, mod_5_1_res, mod_5_2_res, sum_3bits_1_c, sum_3bits_2_c;
  wire [2:2] get_command_1_get, get_command_1_pop;
  wire [3:0] transmission_1_p1;

  not not_1 (not_1_out, transmission_1_p2);
  get_command get_command_1 (
    .command(COMMAND), .push(get_command_1_push), .pop(get_command_1_pop[2]), .get(get_command_1_get[2]));
  // Transmission_Gate #(.width(4)) transmission_1: pin names not known; wires that end beside it: transmission_1_p1, transmission_1_p2, not_1_out, IO_DATA_in
  or or_1 (or_1_out, get_command_1_pop[2], get_command_1_get[2]);
  and and_1 (and_1_out, CLK, or_1_out);
  mod_5 mod_5_1 (.bits(INDEX), .res(mod_5_1_res));
  not not_2 (transmission_1_p2, and_1_out);
  inc_dec_pointer inc_dec_pointer_1 (
    .pop(get_command_1_pop[2]), .push(get_command_1_push), .RESET(RESET), .C(CLK), .res(inc_dec_pointer_1_res));
  assign and_2_out = mod_5_1_res & {3{get_command_1_get[2]}};  // AND_Gate and_2, 3 bits wide
  and and_3 (and_3_out, CLK, get_command_1_push);
  sum_3bits sum_3bits_1 (.a(and_2_out), .b(inc_dec_pointer_1_res), .c(sum_3bits_1_c));
  sum_3bits sum_3bits_2 (.a(sum_3bits_1_c), .b({get_command_1_pop[2], 2'b00}), .c(sum_3bits_2_c));
  mod_5 mod_5_2 (.bits(sum_3bits_2_c), .res(mod_5_2_res));
  getter_setter_stack getter_setter_stack_1 (
    .cell_index_o(mod_5_2_res), .C_o(and_1_out), .cell_index_i(inc_dec_pointer_1_res), .C_i(and_3_out),
    .value(IO_DATA_in), .RESET(RESET), .result(transmission_1_p1), .d0(d0), .d1(d1), .d2(d2), .d3(d3), .d4(d4));

  assign IO_DATA_out = IO_DATA_in;
endmodule

module rs_trigger (
  input  R,
  input  C,
  input  S,
  input  RESET,
  output Q,
  output NQ
);

  wire and_1_out, and_2_out, nor_2_out, or_1_out, por_1_out;

  and and_1 (and_1_out, R, C);
  and and_2 (and_2_out, C, S);
  POR por_1 (.out(por_1_out));
  nor nor_1 (Q, and_1_out, NQ);
  nor nor_2 (nor_2_out, Q, and_2_out);
  or or_1 (or_1_out, RESET, por_1_out);
  or or_2 (NQ, nor_2_out, or_1_out);
endmodule

module d_trigger (
  input  C,
  input  D,
  input  RESET,
  output Q,
  output NQ
);

  wire not_1_out;

  not not_1 (not_1_out, D);
  rs_trigger rs_trigger_1 (.R(not_1_out), .C(C), .S(D), .RESET(RESET), .Q(Q), .NQ(NQ));
endmodule

module pointer (
  input  [2:0] bits_input,
  input  C,
  input  RESET,
  output [2:0] bits_output
);

  d_trigger d_trigger_1 (.C(C), .D(bits_input[0]), .RESET(RESET), .Q(bits_output[0]));  // open: NQ
  d_trigger d_trigger_2 (.C(C), .D(bits_input[1]), .RESET(RESET), .Q(bits_output[1]));  // open: NQ
  d_trigger d_trigger_3 (.C(C), .D(bits_input[2]), .RESET(RESET), .Q(bits_output[2]));  // open: NQ
endmodule

module stack_memory (
  input  [3:0] bits_input_0,
  input  C0,
  input  [3:0] bits_input_1,
  input  C1,
  input  [3:0] bits_input_2,
  input  C2,
  input  [3:0] bits_input_3,
  input  C3,
  input  [3:0] bits_input_4,
  input  C4,
  input  RESET,
  output [3:0] bits_output_0,
  output [3:0] bits_output_1,
  output [3:0] bits_output_2,
  output [3:0] bits_output_3,
  output [3:0] bits_output_4
);

  stack_cell stack_cell_1 (.bits_input(bits_input_0), .C(C0), .RESET(RESET), .bits_output(bits_output_0));
  stack_cell stack_cell_2 (.bits_input(bits_input_1), .C(C1), .RESET(RESET), .bits_output(bits_output_1));
  stack_cell stack_cell_3 (.bits_input(bits_input_2), .C(C2), .RESET(RESET), .bits_output(bits_output_2));
  stack_cell stack_cell_4 (.bits_input(bits_input_3), .C(C3), .RESET(RESET), .bits_output(bits_output_3));
  stack_cell stack_cell_5 (.bits_input(bits_input_4), .C(C4), .RESET(RESET), .bits_output(bits_output_4));
endmodule

module stack_cell (
  input  [3:0] bits_input,
  input  C,
  input  RESET,
  output [3:0] bits_output
);

  d_trigger d_trigger_1 (.C(C), .D(bits_input[0]), .RESET(RESET), .Q(bits_output[0]));  // open: NQ
  d_trigger d_trigger_2 (.C(C), .D(bits_input[1]), .RESET(RESET), .Q(bits_output[1]));  // open: NQ
  d_trigger d_trigger_3 (.C(C), .D(bits_input[2]), .RESET(RESET), .Q(bits_output[2]));  // open: NQ
  d_trigger d_trigger_4 (.C(C), .D(bits_input[3]), .RESET(RESET), .Q(bits_output[3]));  // open: NQ
endmodule

module three_to_five (
  input  bit_0,
  input  bit_1,
  input  bit_2,
  output out_0,
  output out_1,
  output out_2,
  output out_3,
  output out_4
);

  and and_1 (out_0, ~bit_0, ~bit_1, ~bit_2);  // AND_Gate
  and and_2 (out_1, bit_0, ~bit_1, ~bit_2);  // AND_Gate
  and and_3 (out_2, ~bit_0, bit_1, ~bit_2);  // AND_Gate
  and and_4 (out_3, bit_0, bit_1, ~bit_2);  // AND_Gate
  and and_5 (out_4, ~bit_0, ~bit_1, bit_2);  // AND_Gate
endmodule

module get_0000_1111 (
  input  \bit ,
  output [3:0] bits
);


  assign bits = {4{\bit }};
endmodule

module get_5_times_0000_1111 (
  input  bit0,
  input  bit1,
  input  bit2,
  input  bit3,
  input  bit4,
  output [3:0] bits_0,
  output [3:0] bits_1,
  output [3:0] bits_2,
  output [3:0] bits_3,
  output [3:0] bits_4
);

  get_0000_1111 get_0000_1111_1 (.\bit (bit0), .bits(bits_0));
  get_0000_1111 get_0000_1111_2 (.\bit (bit1), .bits(bits_1));
  get_0000_1111 get_0000_1111_3 (.\bit (bit2), .bits(bits_2));
  get_0000_1111 get_0000_1111_4 (.\bit (bit3), .bits(bits_3));
  get_0000_1111 get_0000_1111_5 (.\bit (bit4), .bits(bits_4));
endmodule

module getter_setter_stack (
  input  [2:0] cell_index_o,
  input  C_o,
  input  [2:0] cell_index_i,
  input  C_i,
  input  [3:0] value,
  input  RESET,
  output [3:0] result,
  output [3:0] d0,
  output [3:0] d1,
  output [3:0] d2,
  output [3:0] d3,
  output [3:0] d4
);

  wire or_1_out, or_2_out, or_3_out, or_4_out, three_to_five_1_out_0, three_to_five_1_out_1,
       three_to_five_1_out_2, three_to_five_1_out_3, three_to_five_1_out_4, three_to_five_2_out_0,
       three_to_five_2_out_1, three_to_five_2_out_2, three_to_five_2_out_3, three_to_five_2_out_4;
  wire [3:0] and_1_out, and_2_out, and_3_out, and_4_out, and_5_out, get_5_times_0000_1111_1_bits_0,
       get_5_times_0000_1111_1_bits_1, get_5_times_0000_1111_1_bits_2, get_5_times_0000_1111_1_bits_3,
       get_5_times_0000_1111_1_bits_4;

  or or_1 (or_1_out, cell_index_i[0], ~C_i);  // OR_Gate
  or or_2 (or_2_out, cell_index_i[2], ~C_i);  // OR_Gate
  or or_3 (or_3_out, cell_index_o[0], ~C_o);  // OR_Gate
  or or_4 (or_4_out, cell_index_o[2], ~C_o);  // OR_Gate
  three_to_five three_to_five_1 (
    .bit_0(or_1_out), .bit_1(cell_index_i[1]), .bit_2(or_2_out), .out_0(three_to_five_1_out_0),
    .out_1(three_to_five_1_out_1), .out_2(three_to_five_1_out_2), .out_3(three_to_five_1_out_3),
    .out_4(three_to_five_1_out_4));
  three_to_five three_to_five_2 (
    .bit_0(or_3_out), .bit_1(cell_index_o[1]), .bit_2(or_4_out), .out_0(three_to_five_2_out_0),
    .out_1(three_to_five_2_out_1), .out_2(three_to_five_2_out_2), .out_3(three_to_five_2_out_3),
    .out_4(three_to_five_2_out_4));
  get_5_times_0000_1111 get_5_times_0000_1111_1 (
    .bit0(three_to_five_2_out_0), .bit1(three_to_five_2_out_1), .bit2(three_to_five_2_out_2),
    .bit3(three_to_five_2_out_3), .bit4(three_to_five_2_out_4), .bits_0(get_5_times_0000_1111_1_bits_0),
    .bits_1(get_5_times_0000_1111_1_bits_1), .bits_2(get_5_times_0000_1111_1_bits_2),
    .bits_3(get_5_times_0000_1111_1_bits_3), .bits_4(get_5_times_0000_1111_1_bits_4));
  stack_memory stack_memory_1 (
    .bits_input_0(value), .C0(three_to_five_1_out_0), .bits_input_1(value), .C1(three_to_five_1_out_1),
    .bits_input_2(value), .C2(three_to_five_1_out_2), .bits_input_3(value), .C3(three_to_five_1_out_3),
    .bits_input_4(value), .C4(three_to_five_1_out_4), .RESET(RESET), .bits_output_0(d0), .bits_output_1(d1),
    .bits_output_2(d2), .bits_output_3(d3), .bits_output_4(d4));
  assign and_1_out = d0 & get_5_times_0000_1111_1_bits_0;  // AND_Gate and_1, 4 bits wide
  assign and_2_out = d1 & get_5_times_0000_1111_1_bits_1;  // AND_Gate and_2, 4 bits wide
  assign and_3_out = d2 & get_5_times_0000_1111_1_bits_2;  // AND_Gate and_3, 4 bits wide
  assign and_4_out = d3 & get_5_times_0000_1111_1_bits_3;  // AND_Gate and_4, 4 bits wide
  assign and_5_out = get_5_times_0000_1111_1_bits_4 & d4;  // AND_Gate and_5, 4 bits wide
  assign result = and_1_out | and_2_out | and_3_out | and_4_out | and_5_out;  // OR_Gate or_5, 4 bits wide
endmodule

module half_sum (
  input  b0,
  input  b1,
  output C,
  output S
);

  and and_1 (C, b0, b1);
  xor xor_1 (S, b0, b1);
endmodule

module full_summator (
  input  b0,
  input  b1,
  input  b2,
  output C,
  output S
);

  wire half_sum_1_c, half_sum_1_s, half_sum_2_c;

  half_sum half_sum_1 (.b0(b0), .b1(b1), .C(half_sum_1_c), .S(half_sum_1_s));
  half_sum half_sum_2 (.b0(half_sum_1_s), .b1(b2), .C(half_sum_2_c), .S(S));
  or or_1 (C, half_sum_1_c, half_sum_2_c);
endmodule

module sum_3bits (
  input  [2:0] a,
  input  [2:0] b,
  output [2:0] c
);

  wire full_summator_1_c, full_summator_1_s, full_summator_2_c, half_sum_1_c, half_sum_1_s;

  half_sum half_sum_1 (.b0(a[0]), .b1(b[0]), .C(half_sum_1_c), .S(half_sum_1_s));
  full_summator full_summator_1 (.b0(half_sum_1_c), .b1(a[1]), .b2(b[1]), .C(full_summator_1_c), .S(full_summator_1_s));
  full_summator full_summator_2 (.b0(full_summator_1_c), .b1(a[2]), .b2(b[2]), .C(full_summator_2_c), .S(c[2]));
  or or_1 (c[0], half_sum_1_s, full_summator_2_c);
  or or_2 (c[1], full_summator_1_s, full_summator_2_c);
endmodule

module mod_5 (
  input  [2:0] bits,
  output [2:0] res
);

  wire and_1_out, and_2_out, or_1_out;

  or or_1 (or_1_out, bits[1], bits[0]);
  and and_1 (and_1_out, bits[2], or_1_out);
  and and_2 (and_2_out, ~bits[0], and_1_out);  // AND_Gate
  xor xor_1 (res[0], bits[0], and_1_out);
  xor xor_2 (res[1], bits[1], and_2_out);
  xor xor_3 (res[2], bits[2], and_1_out);
endmodule

module inc_dec_pointer (
  input  pop,
  input  push,
  input  RESET,
  input  C,
  output [2:0] res
);

  wire and_1_out, not_1_out, or_1_out;
  wire [2:0] pointer_1_bits_output, pointer_2_bits_output, sum_3bits_1_c;

  or or_1 (or_1_out, pop, push);
  sum_3bits sum_3bits_1 (.a(pointer_2_bits_output), .b({push, 1'b0, pop}), .c(sum_3bits_1_c));
  and and_1 (and_1_out, or_1_out, C);
  mod_5 mod_5_1 (.bits(sum_3bits_1_c), .res(res));
  pointer pointer_1 (.bits_input(res), .C(and_1_out), .RESET(RESET), .bits_output(pointer_1_bits_output));
  not not_1 (not_1_out, and_1_out);
  pointer pointer_2 (
    .bits_input(pointer_1_bits_output), .C(not_1_out), .RESET(RESET), .bits_output(pointer_2_bits_output));
endmodule

module get_command (
  input  [1:0] command,
  output push,
  output pop,
  output get
);

  and and_1 (push, command[0], ~command[1]);  // AND_Gate
  and and_2 (pop, ~command[0], command[1]);  // AND_Gate
  and and_3 (get, command[0], command[1]);
endmodule
